# Fritzing sketch Fritzing Breadboard (saved by Fritzing 0.9.3b)
breadboards: 1

parts:
  Raspberry_Pi1 = Raspberry Pi B+
  S1 = Momentary Switch [package=ksa_sealed_tac_switch]
  S2 = Momentary Switch [package=ksa_sealed_tac_switch]
  R1 = Resistor [tolerance=±5% resistance=220 package=THT]
  R2 = Resistor [tolerance=±5% resistance=220 package=THT]
  R3 = Resistor [tolerance=±5% resistance=220 package=THT]
  LED3 = LED - 3mm [color="Red (633nm)" package="3 mm [THT]"]
  LED4 = LED - 3mm [color="Red (633nm)" package="3 mm [THT]"]
  LED5 = LED - 3mm [color="Red (633nm)" package="3 mm [THT]"]
  S3 = Pushbutton [package="[THT]"]
  Part1 = BME280 Breakout

nets:
  N1: Raspberry_Pi1.GPIO2, Part1.SDI/SDA
  N2: Raspberry_Pi1.GPIO3, Part1.SCK/SCL
  N3: Raspberry_Pi1.GPIO13, LED5.anode
  N4: Raspberry_Pi1.GPIO19, LED4.anode
  N5: Raspberry_Pi1.GPIO26, LED3.anode
  N6: Raspberry_Pi1.GPIO21, S3.Pin_1, S3.Pin_2
  N7: Raspberry_Pi1.GPIO20, S2.1
  N8: Raspberry_Pi1.GPIO16, S1.1
  N9: S1.4, S2.4, R1.Pin_0, R2.Pin_0, R3.Pin_0, S3.Pin_3, S3.Pin_4
  N10: R1.Pin_1, LED3.cathode
  N11: R2.Pin_1, LED4.cathode
  N12: R3.Pin_1, LED5.cathode
